# Fritzing sketch Connection (saved by Fritzing 0.8.7b)
breadboards: 1

parts:
  Bauteil2 = Arduino Micro (Rev3)
  Bauteil3 = FTDI Basic Programmer

nets:
  N1: Bauteil2.D1/TX, Bauteil3.RXI
  N2: Bauteil2.D0/RX, Bauteil3.TXO
  GND: Bauteil2.GND, Bauteil3.GND
